# Fritzing sketch GeekLogger (saved by Fritzing 0.9.3b)
breadboards: 1

parts:
  GSM_SIM_GPSR_SMS_SIM900_SIM1 = SIM800L [package=THT]
  Part1 = Arduino Micro (Rev3)
  X1 = USB Connectors [package=usb-microb]
  U1 = LIPO-2000mAh [package=lipo-2000]
  Part2 = Power Cell LiPo Charger/Booster
  LED2 = smd LED [color="White (4500K)" package="0603 [SMD]"]
  LM1 = RioRand LM2596
  U2 = 2.4GHz Low Power Transceiver [package=qfn20]
  C1 = Electrolytic Capacitor [capacitance=1000µF package="300 mil [THT, electrolytic]"]

nets:
  GND: GSM_SIM_GPSR_SMS_SIM900_SIM1.GND#1, X1.GND, U1.-, Part2.GND, LED2.cathode, LM1.Pin_1, C1.-
  N1: GSM_SIM_GPSR_SMS_SIM900_SIM1.VDD, LM1.Pin_0
  N2: GSM_SIM_GPSR_SMS_SIM900_SIM1.SIM_TXD, Part1.D0/RX
  N3: GSM_SIM_GPSR_SMS_SIM900_SIM1.SIM_RXD, Part1.D1/TX
  N4: GSM_SIM_GPSR_SMS_SIM900_SIM1.RST, Part1.D4_PWM/A6
  N5: Part1.MOSI, U2.MOSI
  GND_2: Part1.GND, LM1.Pin_3, U2.VSS
  N6: Part1.D5_PWM, LED2.anode
  N7: Part1.D9_PWM/A9, U2.CE
  N8: Part1.D10_PWM/A10, U2.CSN
  N9: Part1.SCK, U2.SCK
  N10: Part1.MISO, U2.MISO
  N11: Part1.5V, X1.VBUS, Part2.5VIN, C1.+
  N12: U1.+, Part2.VBATT
  N13: LM1.Pin_2, U2.VDD
